// Digital circuit ALU.dig as structural Verilog
module ALU (
  input  [7:0] N,
  input  [2:0] OP,
  input  CK,
  input  EN,
  output [7:0] AC_out,
  output [7:0] MQ_out
);

  wire [7:0] S_div, S_left, S_MQdiv, S_MQmul, S_mul, S_muxAC, S_muxMQ, S_nand, S_right, S_soma, S_sub, S_xor;

  soma_8bits soma_8bits_1 (.A(AC_out), .B(N), .Cin(1'b0), .S(S_soma));  // open: OF
  sub_8bits sub_8bits_1 (.A(AC_out), .B(N), .Cin(1'b1), .S(S_sub));  // open: OF
  multiplicador_8bits multiplicador_8bits_1 (.AC(AC_out), .N(N), .AC_out(S_mul), .MQ_out(S_MQmul));  // open: OF
  divisor_8bits divisor_8bits_1 (.AC(AC_out), .N(N), .AC_out(S_div), .MQ_out(S_MQdiv));
  shift_left shift_left_1 (.SL_in(AC_out), .SL_out(S_left));
  shift_right shift_right_1 (.SR_in(AC_out), .SR_out(S_right));
  assign S_nand = ~(AC_out & N);  // NAnd nand_1, 8 bits wide
  assign S_xor = AC_out ^ N;  // XOr xor_1, 8 bits wide
  Multiplexer #(.Selector_Bits(3), .Bits(8)) multiplexer_1 (
    .sel(OP), .in_0(S_soma), .in_1(S_sub), .in_2(S_mul), .in_3(S_div), .in_4(S_left), .in_5(S_right),
    .in_6(S_nand), .in_7(S_xor), .out(S_muxAC));
  Multiplexer #(.Selector_Bits(3), .Bits(8)) multiplexer_2 (
    .sel(OP), .in_0(MQ_out), .in_1(MQ_out), .in_2(S_MQmul), .in_3(S_MQdiv), .in_4(MQ_out), .in_5(MQ_out),
    .in_6(MQ_out), .in_7(MQ_out), .out(S_muxMQ));
  Register #(.Bits(8)) register_1 (.D(S_muxAC), .C(CK), .en(EN), .Q(AC_out));
  Register #(.Bits(8)) register_2 (.D(S_muxMQ), .C(CK), .en(EN), .Q(MQ_out));

  // Other names for the same wires on the sheet: AC[7:0] = AC_out; CL = CK; Q_MQ[7:0] = MQ_out
endmodule
