// Digital circuit CPU.dig as structural Verilog
module CPU (
  input  En,
  input  Clk,
  output [7:0] AC_out,
  output [7:0] MQ_out
);

  wire CLK_en, PC_ovf, Q, Q_t;
  wire [2:0] OP;
  wire [7:0] N, PC_out;
  wire [10:0] rom_1_d;

  and and_1 (CLK_en, Clk, En);
  Counter #(.Bits(8)) PC (.en(Q), .C(Clk), .clr(1'b0), .out(PC_out), .ovf(PC_ovf));
  ROM #(.AddrBits(8), .Bits(11)) rom_1 (.A(PC_out), .sel(Q_t), .D(rom_1_d));
  D_FF d_ff_1 (.D(Q_t), .C(CLK_en), .Q(Q), .nQ(Q_t));
  Register #(.Bits(11)) IR (.D(rom_1_d), .C(Clk), .en(Q_t), .Q({OP, N}));
  ALU alu_1 (.N(N), .OP(OP), .CK(CLK_en), .EN(Q), .AC_out(AC_out), .MQ_out(MQ_out));
  // also tied to GND on the sheet: PC_ovf

  // Notes on the sheet:
  //   contents of rom_1 (hex, n*v repeats v):
  //   2,101,204,303,400,500,6ee,7fc
endmodule
