// Digital circuit divisor_8bits.dig as structural Verilog
module divisor_8bits (
  input  [7:0] AC,
  input  [7:0] N,
  output [7:0] AC_out,
  output [7:0] MQ_out
);

  wire [7:0] S_sub0, S_sub1, S_sub2, S_sub3, S_sub4, S_sub5, S_sub6, S_sub7;
  wire [7:1] A1, A2, A3, A4, A5, A6, A7;
  wire [7:7] Mux_0, Mux_1, Mux_2, Mux_3, Mux_4, Mux_5, Mux_6;

  sub_8bits sub_8bits_1 (.A({{7{1'b0}}, AC[7]}), .B(N), .Cin(1'b1), .S(S_sub0), .OF(MQ_out[7]));
  Multiplexer #(.Bits(8)) multiplexer_1 (
    .sel(MQ_out[7]), .in_0({{7{1'b0}}, AC[7]}), .in_1(S_sub0), .out({Mux_0[7], A1}));
  sub_8bits sub_8bits_2 (.A({A1, AC[6]}), .B(N), .Cin(1'b1), .S(S_sub1), .OF(MQ_out[6]));
  Multiplexer #(.Bits(8)) multiplexer_2 (.sel(MQ_out[6]), .in_0({A1, AC[6]}), .in_1(S_sub1), .out({Mux_1[7], A2}));
  sub_8bits sub_8bits_3 (.A({A2, AC[5]}), .B(N), .Cin(1'b1), .S(S_sub2), .OF(MQ_out[5]));
  Multiplexer #(.Bits(8)) multiplexer_3 (.sel(MQ_out[5]), .in_0({A2, AC[5]}), .in_1(S_sub2), .out({Mux_2[7], A3}));
  sub_8bits sub_8bits_4 (.A({A3, AC[4]}), .B(N), .Cin(1'b1), .S(S_sub3), .OF(MQ_out[4]));
  Multiplexer #(.Bits(8)) multiplexer_4 (.sel(MQ_out[4]), .in_0({A3, AC[4]}), .in_1(S_sub3), .out({Mux_3[7], A4}));
  sub_8bits sub_8bits_5 (.A({A4, AC[3]}), .B(N), .Cin(1'b1), .S(S_sub4), .OF(MQ_out[3]));
  Multiplexer #(.Bits(8)) multiplexer_5 (.sel(MQ_out[3]), .in_0({A4, AC[3]}), .in_1(S_sub4), .out({Mux_4[7], A5}));
  sub_8bits sub_8bits_6 (.A({A5, AC[2]}), .B(N), .Cin(1'b1), .S(S_sub5), .OF(MQ_out[2]));
  Multiplexer #(.Bits(8)) multiplexer_6 (.sel(MQ_out[2]), .in_0({A5, AC[2]}), .in_1(S_sub5), .out({Mux_5[7], A6}));
  sub_8bits sub_8bits_7 (.A({A6, AC[1]}), .B(N), .Cin(1'b1), .S(S_sub6), .OF(MQ_out[1]));
  Multiplexer #(.Bits(8)) multiplexer_7 (.sel(MQ_out[1]), .in_0({A6, AC[1]}), .in_1(S_sub6), .out({Mux_6[7], A7}));
  sub_8bits sub_8bits_8 (.A({A7, AC[0]}), .B(N), .Cin(1'b1), .S(S_sub7), .OF(MQ_out[0]));
  Multiplexer #(.Bits(8)) multiplexer_8 (.sel(MQ_out[0]), .in_0({A7, AC[0]}), .in_1(S_sub7), .out(AC_out));

  // Other names for the same wires on the sheet: A7[0] = AC[0]; AC_0 = AC[0]; A6[0] = AC[1]; AC_1 = AC[1];
  //   A5[0] = AC[2]; AC_2 = AC[2]; A4[0] = AC[3]; AC_3 = AC[3]; A3[0] = AC[4]; AC_4 = AC[4]; A2[0] = AC[5];
  //   AC_5 = AC[5]; A1[0] = AC[6]; AC_6 = AC[6]; A[0] = AC[7]; AC_7 = AC[7]; Mux_0[6:0] = A1; Mux_1[6:0] = A2;
  //   Mux_2[6:0] = A3; Mux_3[6:0] = A4; Mux_4[6:0] = A5; Mux_5[6:0] = A6; Mux_6[6:0] = A7; Mux_7[7:0] = AC_out;
  //   Q0 = MQ_out[0]; Q1 = MQ_out[1]; Q2 = MQ_out[2]; Q3 = MQ_out[3]; Q4 = MQ_out[4]; Q5 = MQ_out[5]; Q6 = MQ_out[6];
  //   Q7 = MQ_out[7]

  // Notes on the sheet:
  //   AC_out: recebe o Resto
  //   MQ_out: recebe o Quociente
endmodule
