// Digital circuit multiplicador_8bits.dig as structural Verilog
module multiplicador_8bits (
  input  [7:0] AC,
  input  [7:0] N,
  output [7:0] AC_out,
  output [7:0] MQ_out,
  output OF
);

  wire [7:0] and_1_out;
  wire [8:1] and_2_out;
  wire [9:2] and_3_out;
  wire [10:3] and_4_out;
  wire [11:4] and_5_out;
  wire [12:5] and_6_out;
  wire [13:6] and_7_out;
  wire [14:7] and_8_out;
  wire [15:0] soma_16bits_1_s, soma_16bits_2_s, soma_16bits_3_s, soma_16bits_4_s, soma_16bits_5_s,
       soma_16bits_6_s;

  assign and_1_out = AC & {8{N[0]}};  // And and_1, 8 bits wide
  assign and_2_out = AC & {8{N[1]}};  // And and_2, 8 bits wide
  assign and_3_out = AC & {8{N[2]}};  // And and_3, 8 bits wide
  soma_16bits soma_16bits_1 (
    .A({{8{1'b0}}, and_1_out}), .B({{7{1'b0}}, and_2_out, 1'b0}), .Cin(1'b0), .S(soma_16bits_1_s));  // open: OF
  assign and_4_out = AC & {8{N[3]}};  // And and_4, 8 bits wide
  soma_16bits soma_16bits_2 (
    .A(soma_16bits_1_s), .B({{6{1'b0}}, and_3_out, 2'b00}), .Cin(1'b0), .S(soma_16bits_2_s));  // open: OF
  assign and_5_out = AC & {8{N[4]}};  // And and_5, 8 bits wide
  assign and_6_out = AC & {8{N[5]}};  // And and_6, 8 bits wide
  soma_16bits soma_16bits_3 (
    .A(soma_16bits_2_s), .B({{5{1'b0}}, and_4_out, 3'b000}), .Cin(1'b0), .S(soma_16bits_3_s));  // open: OF
  soma_16bits soma_16bits_4 (
    .A(soma_16bits_3_s), .B({4'b0000, and_5_out, 4'b0000}), .Cin(1'b0), .S(soma_16bits_4_s));  // open: OF
  assign and_7_out = AC & {8{N[6]}};  // And and_7, 8 bits wide
  soma_16bits soma_16bits_5 (
    .A(soma_16bits_4_s), .B({3'b000, and_6_out, {5{1'b0}}}), .Cin(1'b0), .S(soma_16bits_5_s));  // open: OF
  assign and_8_out = AC & {8{N[7]}};  // And and_8, 8 bits wide
  soma_16bits soma_16bits_6 (
    .A(soma_16bits_5_s), .B({2'b00, and_7_out, {6{1'b0}}}), .Cin(1'b0), .S(soma_16bits_6_s));  // open: OF
  soma_16bits soma_16bits_7 (
    .A(soma_16bits_6_s), .B({1'b0, and_8_out, {7{1'b0}}}), .Cin(1'b0), .S({MQ_out, AC_out}), .OF(OF));

  // Notes on the sheet:
  //   Saída: soma parcial de AC + N0
endmodule
