// Digital circuit soma_16bits.dig as structural Verilog
module soma_16bits (
  input  [15:0] A,
  input  [15:0] B,
  input  Cin,
  output [15:0] S,
  output OF
);

  wire soma_1bit_1_co, soma_1bit_2_co, soma_1bit_3_co, soma_1bit_4_co, soma_1bit_5_co, soma_1bit_6_co,
       soma_1bit_7_co, soma_1bit_8_co, soma_1bit_9_co, soma_1bit_10_co, soma_1bit_11_co, soma_1bit_12_co,
       soma_1bit_13_co, soma_1bit_14_co, soma_1bit_15_co;

  soma_1bit soma_1bit_1 (.A(A[0]), .B(B[0]), .Cin(Cin), .S(S[0]), .Co(soma_1bit_1_co));
  soma_1bit soma_1bit_2 (.A(A[1]), .B(B[1]), .Cin(soma_1bit_1_co), .S(S[1]), .Co(soma_1bit_2_co));
  soma_1bit soma_1bit_3 (.A(A[2]), .B(B[2]), .Cin(soma_1bit_2_co), .S(S[2]), .Co(soma_1bit_3_co));
  soma_1bit soma_1bit_4 (.A(A[3]), .B(B[3]), .Cin(soma_1bit_3_co), .S(S[3]), .Co(soma_1bit_4_co));
  soma_1bit soma_1bit_5 (.A(A[4]), .B(B[4]), .Cin(soma_1bit_4_co), .S(S[4]), .Co(soma_1bit_5_co));
  soma_1bit soma_1bit_6 (.A(A[5]), .B(B[5]), .Cin(soma_1bit_5_co), .S(S[5]), .Co(soma_1bit_6_co));
  soma_1bit soma_1bit_7 (.A(A[6]), .B(B[6]), .Cin(soma_1bit_6_co), .S(S[6]), .Co(soma_1bit_7_co));
  soma_1bit soma_1bit_8 (.A(A[7]), .B(B[7]), .Cin(soma_1bit_7_co), .S(S[7]), .Co(soma_1bit_8_co));
  soma_1bit soma_1bit_9 (.A(A[8]), .B(B[8]), .Cin(soma_1bit_8_co), .S(S[8]), .Co(soma_1bit_9_co));
  soma_1bit soma_1bit_10 (.A(A[9]), .B(B[9]), .Cin(soma_1bit_9_co), .S(S[9]), .Co(soma_1bit_10_co));
  soma_1bit soma_1bit_11 (.A(A[10]), .B(B[10]), .Cin(soma_1bit_10_co), .S(S[10]), .Co(soma_1bit_11_co));
  soma_1bit soma_1bit_12 (.A(A[11]), .B(B[11]), .Cin(soma_1bit_11_co), .S(S[11]), .Co(soma_1bit_12_co));
  soma_1bit soma_1bit_13 (.A(A[12]), .B(B[12]), .Cin(soma_1bit_12_co), .S(S[12]), .Co(soma_1bit_13_co));
  soma_1bit soma_1bit_14 (.A(A[13]), .B(B[13]), .Cin(soma_1bit_13_co), .S(S[13]), .Co(soma_1bit_14_co));
  soma_1bit soma_1bit_15 (.A(A[14]), .B(B[14]), .Cin(soma_1bit_14_co), .S(S[14]), .Co(soma_1bit_15_co));
  soma_1bit soma_1bit_16 (.A(A[15]), .B(B[15]), .Cin(soma_1bit_15_co), .S(S[15]), .Co(OF));
endmodule
