// Digital circuit soma_8bits.dig as structural Verilog
module soma_8bits (
  input  [7:0] A,
  input  [7:0] B,
  input  Cin,
  output [7:0] S,
  output OF
);

  wire soma_1bit_1_co, soma_1bit_2_co, soma_1bit_3_co, soma_1bit_4_co, soma_1bit_5_co, soma_1bit_6_co,
       soma_1bit_7_co;

  soma_1bit soma_1bit_1 (.A(A[0]), .B(B[0]), .Cin(Cin), .S(S[0]), .Co(soma_1bit_1_co));
  soma_1bit soma_1bit_2 (.A(A[1]), .B(B[1]), .Cin(soma_1bit_1_co), .S(S[1]), .Co(soma_1bit_2_co));
  soma_1bit soma_1bit_3 (.A(A[2]), .B(B[2]), .Cin(soma_1bit_2_co), .S(S[2]), .Co(soma_1bit_3_co));
  soma_1bit soma_1bit_4 (.A(A[3]), .B(B[3]), .Cin(soma_1bit_3_co), .S(S[3]), .Co(soma_1bit_4_co));
  soma_1bit soma_1bit_5 (.A(A[4]), .B(B[4]), .Cin(soma_1bit_4_co), .S(S[4]), .Co(soma_1bit_5_co));
  soma_1bit soma_1bit_6 (.A(A[5]), .B(B[5]), .Cin(soma_1bit_5_co), .S(S[5]), .Co(soma_1bit_6_co));
  soma_1bit soma_1bit_7 (.A(A[6]), .B(B[6]), .Cin(soma_1bit_6_co), .S(S[6]), .Co(soma_1bit_7_co));
  soma_1bit soma_1bit_8 (.A(A[7]), .B(B[7]), .Cin(soma_1bit_7_co), .S(S[7]), .Co(OF));
endmodule
