// Digital circuit sub_8bits.dig as structural Verilog
module sub_8bits (
  input  [7:0] A,
  input  [7:0] B,
  input  Cin,
  output [7:0] S,
  output OF
);

  wire B0, B1, B2, B3, B4, B5, B6, B7, soma_1bit_1_co, soma_1bit_2_co, soma_1bit_3_co, soma_1bit_4_co,
       soma_1bit_5_co, soma_1bit_6_co, soma_1bit_7_co;

  not not_1 (B0, B[0]);
  not not_2 (B1, B[1]);
  not not_3 (B2, B[2]);
  not not_4 (B3, B[3]);
  not not_5 (B4, B[4]);
  not not_6 (B5, B[5]);
  not not_7 (B6, B[6]);
  not not_8 (B7, B[7]);
  soma_1bit soma_1bit_1 (.A(A[0]), .B(B0), .Cin(Cin), .S(S[0]), .Co(soma_1bit_1_co));
  soma_1bit soma_1bit_2 (.A(A[1]), .B(B1), .Cin(soma_1bit_1_co), .S(S[1]), .Co(soma_1bit_2_co));
  soma_1bit soma_1bit_3 (.A(A[2]), .B(B2), .Cin(soma_1bit_2_co), .S(S[2]), .Co(soma_1bit_3_co));
  soma_1bit soma_1bit_4 (.A(A[3]), .B(B3), .Cin(soma_1bit_3_co), .S(S[3]), .Co(soma_1bit_4_co));
  soma_1bit soma_1bit_5 (.A(A[4]), .B(B4), .Cin(soma_1bit_4_co), .S(S[4]), .Co(soma_1bit_5_co));
  soma_1bit soma_1bit_6 (.A(A[5]), .B(B5), .Cin(soma_1bit_5_co), .S(S[5]), .Co(soma_1bit_6_co));
  soma_1bit soma_1bit_7 (.A(A[6]), .B(B6), .Cin(soma_1bit_6_co), .S(S[6]), .Co(soma_1bit_7_co));
  soma_1bit soma_1bit_8 (.A(A[7]), .B(B7), .Cin(soma_1bit_7_co), .S(S[7]), .Co(OF));
endmodule
